# Fritzing sketch 21 (saved by Fritzing 0.9.3b)
breadboards: 5

parts:
  J14 = female pin header, 3 pins [form="♀ (female)"]
  J15 = female pin header, 3 pins [form="♀ (female)"]
  Q1 = PNP-Transistor [package="TO92 [THT]"]
  J33 = female pin header, 3 pins [form="♀ (female)"]
  J34 = female pin header, 3 pins [form="♀ (female)"]
  D2 = Rectifier Diode [part_number=1N4001 package="300 mil [THT]"]
  J35 = female pin header, 3 pins [form="♀ (female)"]
  J36 = female pin header, 3 pins [form="♀ (female)"]
  D3 = Rectifier Diode [part_number=1N4001 package="300 mil [THT]"]
  J37 = female pin header, 3 pins [form="♀ (female)"]
  J39 = female pin header, 4 pins [form="♀ (female)"]
  R1 = Resistor [tolerance=±5% resistance=10k package=THT]
  J40 = female pin header, 3 pins [form="♀ (female)"]
  J41 = female pin header, 3 pins [form="♀ (female)"]
  R2 = Resistor [tolerance=±5% resistance=10k package=THT]
  J43 = female pin header, 4 pins [form="♀ (female)"]
  J44 = female pin header, 4 pins [form="♀ (female)"]
  J45 = female pin header, 3 pins [form="♀ (female)"]
  J46 = female pin header, 3 pins [form="♀ (female)"]
  J47 = female pin header, 4 pins [form="♀ (female)"]
  J48 = female pin header, 3 pins [form="♀ (female)"]
  J49 = female pin header, 3 pins [form="♀ (female)"]
  R3 = Resistor [tolerance=±5% resistance=470 package=THT]
  D4 = Rectifier Diode [part_number=1N4001 package="300 mil [THT]"]
  J51 = female pin header, 3 pins [form="♀ (female)"]
  J53 = female pin header, 3 pins [form="♀ (female)"]
  J54 = female pin header, 3 pins [form="♀ (female)"]
  R4 = Resistor [tolerance=±5% resistance=22k package=THT]
  J55 = female pin header, 4 pins [form="♀ (female)"]
  J56 = female pin header, 4 pins [form="♀ (female)"]
  J57 = female pin header, 4 pins [form="♀ (female)"]
  Q2 = NPN-Transistor [package="TO92 [THT]"]
  J58 = female pin header, 3 pins [form="♀ (female)"]
  J59 = female pin header, 3 pins [form="♀ (female)"]
  LED1 = LED - 5mm [color="Red (633nm)" package="5 mm [THT]"]
  J60 = female pin header, 3 pins [form="♀ (female)"]
  J61 = female pin header, 3 pins [form="♀ (female)"]
  J62 = female pin header, 4 pins [form="♀ (female)"]
  J63 = female pin header, 3 pins [form="♀ (female)"]
  J64 = female pin header, 5 pins [form="♀ (female)"]
  J65 = female pin header, 3 pins [form="♀ (female)"]
  J66 = female pin header, 5 pins [form="♀ (female)"]
  J69 = female pin header, 3 pins [form="♀ (female)"]
  J70 = female pin header, 3 pins [form="♀ (female)"]
  J71 = female pin header, 3 pins [form="♀ (female)"]
  J74 = female pin header, 4 pins [form="♀ (female)"]
  J75 = female pin header, 3 pins [form="♀ (female)"]
  J77 = female pin header, 3 pins [form="♀ (female)"]
  J78 = female pin header, 3 pins [form="♀ (female)"]
  J79 = female pin header, 5 pins [form="♀ (female)"]
  J80 = female pin header, 4 pins [form="♀ (female)"]
  J82 = female pin header, 3 pins [form="♀ (female)"]
  J85 = female pin header, 3 pins [form="♀ (female)"]
  J81 = female pin header, 4 pins [form="♀ (female)"]
  J86 = female pin header, 4 pins [form="♀ (female)"]
  J87 = female pin header, 5 pins [form="♀ (female)"]
  J88 = female pin header, 4 pins [form="♀ (female)"]
  J89 = female pin header, 3 pins [form="♀ (female)"]
  J90 = female pin header, 4 pins [form="♀ (female)"]
  J93 = female pin header, 4 pins [form="♀ (female)"]
  J94 = female pin header, 4 pins [form="♀ (female)"]
  J84 = female pin header, 3 pins [form="♀ (female)"]
  J95 = female pin header, 4 pins [form="♀ (female)"]

nets:
  N1: J14.pin1, J14.pin2, J14.pin3, J15.pin1, J15.pin2, J15.pin3, Q1.E, Q1.C, R1.Pin_0, R1.Pin_1, J45.pin1, J46.pin1, D4.cathode, J54.pin1, J54.pin2, J54.pin3, R4.Pin_1, Q2.B, J58.pin2, J59.pin2, J62.pin1, J62.pin4, J65.pin2, J66.pin4, J69.pin2, J70.pin1, J70.pin3, J71.pin1, J71.pin3, J74.pin1, J74.pin4, J75.pin1, J75.pin3, J79.pin1, J79.pin5, J82.pin1, J82.pin3, J81.pin3, J86.pin2, J87.pin1, J87.pin5, J88.pin2, J89.pin1, J89.pin3, J90.pin1, J90.pin2, J90.pin4, J93.pin1, J93.pin4, J94.pin1, J94.pin4, J95.pin1, J95.pin4
  N2: Q1.B, J33.pin1, J34.pin1, D2.cathode, J35.pin3, J36.pin3, D3.cathode, J37.pin1, J37.pin3, J39.pin1, J39.pin4, J41.pin1, J41.pin2, J41.pin3, R2.Pin_1, J51.pin1, J51.pin3, J62.pin3, J69.pin1, J69.pin3, J70.pin2, J71.pin2, J75.pin2, J80.pin1, J80.pin4, J81.pin1, J81.pin2, J81.pin4, J86.pin1, J86.pin4, J88.pin1, J88.pin4, J94.pin2
  N3: J33.pin2, J34.pin2, J39.pin3
  N4: J33.pin3, J34.pin3, D2.anode, J39.pin2
  N5: J35.pin1, J36.pin1, D3.anode
  N6: J35.pin2, J36.pin2
  N7: J40.pin1, J40.pin2, J40.pin3, R2.Pin_0, J43.pin1, J43.pin4, J44.pin1, J44.pin4, J45.pin3, J46.pin3, D4.anode, J53.pin1, J53.pin2, J53.pin3, R4.Pin_0, J55.pin1, J55.pin4, J56.pin1, J56.pin4, Q2.E, J58.pin1, J59.pin1, J65.pin1, J65.pin3, J66.pin1, J66.pin5, J85.pin1, J85.pin3, J87.pin2, J87.pin4, J89.pin2, J84.pin1, J84.pin3
  N8: J45.pin2, J46.pin2
  N9: J47.pin1, J47.pin4, J48.pin3, J49.pin3, R3.Pin_0
  N10: J48.pin1, J49.pin1, R3.Pin_1, J57.pin1, J57.pin4, LED1.anode, J60.pin3, J61.pin3, J78.pin1, J78.pin3
  N11: J48.pin2, J49.pin2
  N12: Q2.C, J58.pin3, J59.pin3
  N13: LED1.cathode, J60.pin1, J61.pin1, J63.pin1, J63.pin3, J64.pin1, J64.pin5, J77.pin1, J77.pin3
  N14: J60.pin2, J61.pin2
  N15: J62.pin2, J88.pin3
  N16: J86.pin3, J94.pin3
  N17: J87.pin3, J84.pin2

// code stored in the sketch: ªµvµ·-Ω-¼°Φ·µ°.ino

